// Logisim project PW_1_Wizard_Logisim.circ as structural Verilog: 2 circuits, main circuit main
module main (
  input  Run_Reset,
  output [7:0] TestPin
);

  wire Clk_out, MainCPU_output_2;
  wire [7:0] and_1_out, MainMem_dout;
  wire [7:7] MainCPU_ldmem;
  wire [15:0] MainCPU_output_bus_2;

  Clock Clk (.out(Clk_out));
  RAM #(.addrWidth(16), .enables("line"), .\type ("nonvolatile")) MainMem (
    .addr(MainCPU_output_bus_2), .we(MainCPU_output_2), .clk(Clk_out), .din(TestPin), .dout(MainMem_dout));
  PW_1 MainCPU (
    .DataIn(and_1_out), .Clk(Clk_out), .CPUEn(Run_Reset), .LdMem(MainCPU_ldmem[7]),
    .Output_2(MainCPU_output_2), .Output_bus_1(TestPin), .Output_bus_2(MainCPU_output_bus_2));
  assign and_1_out = MainMem_dout & {8{MainCPU_ldmem[7]}};  // AND_Gate and_1, 8 bits wide
endmodule

module PW_1 (
  input  [7:0] DataIn,
  input  Clk,
  input  CPUEn,
  output LdMem,
  output Output_2,
  output [7:0] Output_bus_1,
  output [15:0] Output_bus_2
);

  wire ADD_ADC_out, adder_2_cout, ALU_out, and_1_out, and_2_out, and_3_out, and_4_out, and_5_out, and_6_out,
       and_7_out, and_8_out, and_9_out, and_10_out, and_11_out, and_12_out, BIZ_out, BRANCH_out, CACT_out,
       CALL_out, CRY_q, decoder_1_out0, decoder_1_out1, decoder_1_out2, decoder_1_out3, decoder_2_out0,
       decoder_2_out1, decoder_2_out2, decoder_2_out3, JB_out, JBM_out, LDA_out, LDI_out, Load_out, MEM_out,
       MOV_out, nor_1_out, not_1_out, not_2_out, not_3_out, not_4_out, not_5_out, not_6_out, not_7_out,
       not_8_out, or_1_out, or_2_out, or_3_out, or_4_out, or_5_out, or_6_out, or_7_out, or_9_out, STRA_out,
       t_ff_1_q, t_ff_2_q, t_ff_2_qn, Write_out, xor_1_out;
  wire [1:0] CurrentOp_q_2, CurrentOp_q_3;
  wire [7:0] A_q, adder_1_out, adder_2_out, adder_2_out_2, B_q, C_q, multiplexer_3_out, multiplexer_4_out,
       multiplexer_5_out, multiplexer_7_out, multiplexer_8_out, multiplexer_10_out, multiplexer_11_out,
       nand_1_out, or_8_out, SEG_q, TA_q, TB_q, TC_q, TD_q, xor_2_out;
  wire [7:2] CurrentOp_q;
  wire [8:0] multiplexer_1_out, multiplexer_2_out;
  wire [8:8] adder_1_cout;
  wire [15:0] CTR_q, multiplexer_6_out;

  xor xor_1 (xor_1_out, CPUEn, adder_2_cout);
  T_Flip_Flop t_ff_1 (.T(xor_1_out), .clk(Clk), .Q(t_ff_1_q), .reset(not_1_out));  // open: Qn, preset
  not not_1 (not_1_out, CPUEn);
  T_Flip_Flop t_ff_2 (.T(t_ff_1_q), .clk(Clk), .Q(t_ff_2_q), .Qn(t_ff_2_qn), .reset(not_2_out));  // open: preset
  not not_2 (not_2_out, CPUEn);
  and Load (Load_out, t_ff_1_q, xor_1_out, t_ff_2_qn);
  and Write (Write_out, t_ff_1_q, xor_1_out, t_ff_2_q);
  Register CurrentOp (
    .D(DataIn), .en(Load_out), .clk(Clk), .Q({CurrentOp_q[7:5], CurrentOp_q_2, CurrentOp_q[2], CurrentOp_q_3}));  // open: clr
  nor MOV (MOV_out, CurrentOp_q[7], CurrentOp_q[6]);
  and LDI (LDI_out, CurrentOp_q[7], CurrentOp_q[6]);
  and ALU (ALU_out, ~CurrentOp_q[7], CurrentOp_q[6]);  // AND_Gate
  and JBM (JBM_out, CurrentOp_q[7], ~CurrentOp_q[6]);  // AND_Gate
  not not_3 (not_3_out, CurrentOp_q[7]);
  not not_4 (not_4_out, CurrentOp_q[5]);
  not not_5 (not_5_out, CurrentOp_q[2]);
  and MEM (MEM_out, JBM_out, not_4_out);
  and JB (JB_out, JBM_out, CurrentOp_q[5]);
  and CACT (CACT_out, ALU_out, Write_out);
  and LDA (LDA_out, MEM_out, not_5_out);
  and STRA (STRA_out, MEM_out, CurrentOp_q[2]);
  and BIZ (BIZ_out, JB_out, not_5_out);
  and CALL (CALL_out, or_3_out, Write_out);
  and ADD_ADC (ADD_ADC_out, CRY_q, CurrentOp_q[2]);
  Adder adder_1 (.a(Output_bus_1), .b(or_8_out), .out(adder_1_out), .cin(ADD_ADC_out), .cout(adder_1_cout[8]));
  assign nand_1_out = ~(Output_bus_1 & or_8_out);  // NAND_Gate nand_1, 8 bits wide
  assign xor_2_out = Output_bus_1 ^ or_8_out;  // XOR_Gate xor_2, 8 bits wide
  Multiplexer #(.width(9)) multiplexer_1 (
    .in0({1'b1, nand_1_out}), .in1({1'b1, xor_2_out}), .out(multiplexer_1_out), .sel(CurrentOp_q[2]));
  nor nor_1 (nor_1_out, Output_bus_1[0], Output_bus_1[1], Output_bus_1[2], Output_bus_1[3], Output_bus_1[5], Output_bus_1[6], Output_bus_1[7], Output_bus_1[4]);
  and BRANCH (BRANCH_out, nor_1_out, BIZ_out);
  Multiplexer #(.width(9)) multiplexer_2 (
    .in0({adder_1_cout[8], adder_1_out}), .in1(multiplexer_1_out), .out(multiplexer_2_out),
    .sel(CurrentOp_q[5]));
  or or_1 (or_1_out, LDA_out, LDI_out);
  Multiplexer #(.width(8)) multiplexer_3 (
    .in0(or_8_out), .in1(multiplexer_2_out[7:0]), .out(multiplexer_3_out), .sel(ALU_out));
  or or_2 (or_2_out, not_3_out, CurrentOp_q[6], LDA_out);
  and and_1 (and_1_out, Write_out, ~and_4_out, or_2_out);  // AND_Gate
  and and_2 (and_2_out, xor_1_out, and_1_out);
  Decoder #(.select(2)) decoder_1 (
    .out0(decoder_1_out0), .out1(decoder_1_out1), .out2(decoder_1_out2), .out3(decoder_1_out3),
    .sel(CurrentOp_q_2), .en(and_2_out));
  Multiplexer #(.width(8)) multiplexer_4 (
    .in0(multiplexer_3_out), .in1(DataIn), .out(multiplexer_4_out), .sel(or_1_out));
  Multiplexer #(.width(8)) multiplexer_5 (.in0(Output_bus_1), .in1(SEG_q), .out(multiplexer_5_out), .sel(BRANCH_out));
  and and_3 (and_3_out, xor_1_out, Write_out, and_4_out);
  Decoder #(.select(2)) decoder_2 (
    .out0(decoder_2_out0), .out1(decoder_2_out1), .out2(decoder_2_out2), .out3(decoder_2_out3),
    .sel(CurrentOp_q_2), .en(and_3_out));
  and and_4 (and_4_out, CurrentOp_q[5], MOV_out);
  not not_6 (not_6_out, not_5_out);
  and and_5 (and_5_out, JB_out, not_6_out);
  and and_6 (and_6_out, JB_out, BRANCH_out);
  or or_3 (or_3_out, and_5_out, and_6_out);
  or or_4 (or_4_out, or_3_out, LDI_out);
  and and_7 (and_7_out, or_4_out, Write_out);
  or or_5 (or_5_out, decoder_1_out1, CALL_out);
  or or_6 (or_6_out, decoder_1_out2, CALL_out);
  and and_8 (and_8_out, or_3_out, ~Load_out);  // AND_Gate
  Multiplexer #(.width(16)) multiplexer_6 (
    .in0({adder_2_out_2, adder_2_out}), .in1({multiplexer_5_out, or_8_out}), .out(multiplexer_6_out),
    .sel(and_8_out));
  and and_9 (and_9_out, xor_1_out, or_7_out);
  or or_7 (or_7_out, and_7_out, Load_out);
  Register A (.D(multiplexer_4_out), .en(decoder_1_out0), .clk(Clk), .Q(A_q));  // open: clr
  Register B (.D(multiplexer_7_out), .en(or_5_out), .clk(Clk), .Q(B_q));  // open: clr
  Multiplexer #(.width(8)) multiplexer_7 (
    .in0(multiplexer_4_out), .in1(adder_2_out), .out(multiplexer_7_out), .sel(CALL_out));
  Register C (.D(multiplexer_8_out), .en(or_6_out), .clk(Clk), .Q(C_q));  // open: clr
  Multiplexer #(.width(8)) multiplexer_8 (
    .in0(multiplexer_4_out), .in1(adder_2_out_2), .out(multiplexer_8_out), .sel(CALL_out));
  Register SEG (.D(multiplexer_4_out), .en(decoder_1_out3), .clk(Clk), .Q(SEG_q));  // open: clr
  Register TA (.D(multiplexer_4_out), .en(decoder_2_out0), .clk(Clk), .Q(TA_q));  // open: clr
  Register TB (.D(multiplexer_4_out), .en(decoder_2_out1), .clk(Clk), .Q(TB_q));  // open: clr
  Register TC (.D(multiplexer_4_out), .en(decoder_2_out2), .clk(Clk), .Q(TC_q));  // open: clr
  Register TD (.D(multiplexer_4_out), .en(decoder_2_out3), .clk(Clk), .Q(TD_q));  // open: clr
  Register #(.width(1)) CRY (.D(multiplexer_2_out[8]), .en(CACT_out), .clk(Clk), .Q(CRY_q));  // open: clr
  Register #(.width(16)) CTR (.D(multiplexer_6_out), .en(and_9_out), .clk(Clk), .Q(CTR_q), .clr(not_7_out));
  not not_7 (not_7_out, CPUEn);
  and and_10 (and_10_out, CurrentOp_q[2], MOV_out);
  Multiplexer #(.select(2), .width(8)) multiplexer_9 (
    .in0(A_q), .in1(B_q), .in2(C_q), .in3(SEG_q), .out(Output_bus_1), .sel(CurrentOp_q_2));
  Adder #(.width(16)) adder_2 (
    .a(CTR_q), .b({16{1'b0}}), .out({adder_2_out_2, adder_2_out}), .cin(1'b1), .cout(adder_2_cout));
  not not_8 (not_8_out, and_10_out);
  Multiplexer #(.enable("true"), .select(2), .width(8)) multiplexer_10 (
    .in0(TA_q), .in1(TB_q), .in2(TC_q), .in3(TD_q), .out(multiplexer_10_out), .sel(CurrentOp_q_3),
    .en(and_10_out));
  assign or_8_out = multiplexer_11_out | multiplexer_10_out;  // OR_Gate or_8, 8 bits wide
  Multiplexer #(.enable("true"), .select(2), .width(8)) multiplexer_11 (
    .in0(A_q), .in1(B_q), .in2(C_q), .in3(SEG_q), .out(multiplexer_11_out), .sel(CurrentOp_q_3),
    .en(not_8_out));
  and and_11 (and_11_out, MEM_out, t_ff_2_q);
  Multiplexer #(.width(16)) multiplexer_12 (.in0(CTR_q), .in1({SEG_q, or_8_out}), .out(Output_bus_2), .sel(and_11_out));
  or or_9 (or_9_out, LDI_out, LDA_out);
  and and_12 (and_12_out, or_9_out, t_ff_2_q);
  and and_13 (Output_2, STRA_out, t_ff_2_q);
  or or_10 (LdMem, t_ff_2_qn, and_12_out);
endmodule
