// Logisim project PW_1x2_Doppelwizard.circ as structural Verilog: 2 circuits, main circuit main
module main (
);

  wire and_1_out, and_2_out, and_3_out, and_4_out, and_5_out, and_6_out, and_7_out, and_8_out, and_9_out,
       and_10_out, and_11_out, and_12_out, and_13_out, and_14_out, and_15_out, and_16_out, and_17_out,
       and_18_out, and_19_out, and_20_out, and_21_out, and_22_out, and_23_out, and_24_out, and_25_out,
       and_26_out, and_27_out, and_28_out, and_29_out, and_30_out, and_31_out, and_32_out, and_33_out,
       and_34_out, BIOSLdColCheck_out, clock_1_out, Colision_out, comparator_1_eq, comparator_2_eq,
       comparator_3_eq, comparator_4_eq, comparator_5_eq, comparator_6_eq, comparator_7_eq, comparator_8_eq,
       comparator_9_eq, comparator_10_eq, comparator_11_eq, comparator_12_eq, comparator_13_eq,
       comparator_14_eq, comparator_15_eq, Core0_ldmem, Core0_wrtmem, Core1_ldmem, Core1_wrtmem, d_ff_1_q,
       d_ff_1_qn, d_ff_2_q, Decider_q, Mem0Col_out, Mem1Col_out, multiplexer_1_out, multiplexer_2_out,
       nor_1_out, nor_2_out, not_1_out, or_1_out, or_2_out, or_3_out, or_5_out, or_6_out, or_7_out, or_8_out,
       or_9_out, or_10_out, or_11_out, t_ff_1_q, t_ff_2_q;
  wire [0:0] pull_resistor_5_node, pull_resistor_6_node;
  wire [1:0] Core0_adrout_2, Core1_adrout_2;
  wire [6:0] bit_extender_1_out, keyboard_1_data, pull_resistor_5_node_2, pull_resistor_6_node_2;
  wire [7:0] AtomCore0Ctr_q, AtomCore0High8_q, AtomCore0Low8_q, AtomCore1Ctr_q, AtomCore1High8_q,
       AtomCore1Low8_q, BIOS_data, bit_extender_2_out, Core0_dataout, Core1_dataout, MainMem0_dout,
       MainMem1_dout, multiplexer_4_out, multiplexer_6_out, or_4_out, pull_resistor_1_node,
       pull_resistor_2_node, pull_resistor_3_node, pull_resistor_4_node;
  wire [13:0] Core0_adrout, Core1_adrout, multiplexer_3_out, multiplexer_5_out, multiplexer_7_out;

  Clock clock_1 (.out(clock_1_out));
  Pull_Resistor pull_resistor_1 (.node(pull_resistor_1_node));
  not not_1 (not_1_out, Decider_q);
  Register #(.trigger("falling"), .width(1)) Decider (
    .D(not_1_out), .en(and_1_out), .clk(clock_1_out), .Q(Decider_q));  // open: clr
  D_Flip_Flop d_ff_1 (
    .D(and_2_out), .clk(clock_1_out), .Q(d_ff_1_q), .Qn(d_ff_1_qn), .preset(and_2_out));  // open: reset
  D_Flip_Flop d_ff_2 (.D(d_ff_1_q), .clk(clock_1_out), .Q(d_ff_2_q), .preset(and_2_out));  // open: Qn, reset
  PW_1A Core0 (
    .DataIn(pull_resistor_1_node), .Clk(clock_1_out), .CPUStop(multiplexer_1_out), .CPUEn(1'b1),
    .LdMem(Core0_ldmem), .WrtMem(Core0_wrtmem), .DataOut(Core0_dataout),
    .AdrOut({Core0_adrout_2, Core0_adrout}));
  Multiplexer multiplexer_1 (.in0(or_1_out), .in1(or_10_out), .out(multiplexer_1_out), .sel(or_2_out));
  or or_1 (or_1_out, ~and_2_out, not_1_out);  // OR_Gate
  and and_1 (and_1_out, d_ff_1_qn, d_ff_2_q);
  Pull_Resistor pull_resistor_2 (.node(pull_resistor_2_node));
  Multiplexer multiplexer_2 (.in0(or_3_out), .in1(or_11_out), .out(multiplexer_2_out), .sel(or_2_out));
  or or_2 (or_2_out, or_10_out, or_11_out);
  or or_3 (or_3_out, ~and_2_out, Decider_q);  // OR_Gate
  and and_2 (and_2_out, ~or_10_out, Colision_out, ~or_11_out);  // AND_Gate
  PW_1A Core1 (
    .DataIn(pull_resistor_2_node), .Clk(clock_1_out), .CPUStop(multiplexer_2_out), .CPUEn(1'b1),
    .LdMem(Core1_ldmem), .WrtMem(Core1_wrtmem), .DataOut(Core1_dataout),
    .AdrOut({Core1_adrout_2, Core1_adrout}));
  nor nor_1 (nor_1_out, Core0_adrout_2[1], Core0_adrout_2[0]);
  nor nor_2 (nor_2_out, Core1_adrout_2[1], Core1_adrout_2[0]);
  and BIOSLdColCheck (BIOSLdColCheck_out, nor_1_out, nor_2_out, Core0_ldmem, Core1_ldmem);
  or Colision (Colision_out, BIOSLdColCheck_out, Mem0Col_out, Mem1Col_out);
  Comparator #(.mode("unsigned"), .width(16)) comparator_1 (
    .a({Core1_adrout_2, Core1_adrout}), .b(16'h4000), .eq(comparator_1_eq));  // open: gt, lt
  Comparator #(.mode("unsigned"), .width(16)) comparator_2 (
    .a(16'h4000), .b({Core0_adrout_2, Core0_adrout}), .eq(comparator_2_eq));  // open: gt, lt
  and and_3 (and_3_out, Core0_adrout_2[1], Core1_adrout_2[1]);
  and Mem0Col (Mem0Col_out, and_3_out, ~Core0_adrout[0], ~Core1_adrout[0]);  // AND_Gate
  and and_4 (and_4_out, Core1_wrtmem, comparator_1_eq, multiplexer_2_out);
  and and_5 (and_5_out, Core0_wrtmem, comparator_2_eq, multiplexer_1_out);
  and Mem1Col (Mem1Col_out, and_3_out, Core0_adrout[0], Core1_adrout[0]);
  Bit_Extender #(.out_width(7), .\type ("zero")) bit_extender_1 (.in(or_4_out), .out(bit_extender_1_out));
  assign or_4_out = pull_resistor_3_node | pull_resistor_4_node;  // OR_Gate or_4, 8 bits wide
  Pull_Resistor pull_resistor_3 (.node(pull_resistor_3_node));
  Pull_Resistor pull_resistor_4 (.node(pull_resistor_4_node));
  or or_5 (or_5_out, and_4_out, and_5_out);
  assign pull_resistor_3_node = and_4_out ? Core1_dataout : 8'bz;  // Controlled_Buffer controlled_buffer_1
  assign pull_resistor_4_node = and_5_out ? Core0_dataout : 8'bz;  // Controlled_Buffer controlled_buffer_2
  and and_6 (and_6_out, multiplexer_2_out, Core1_ldmem);
  Multiplexer #(.width(14)) multiplexer_3 (
    .in0(Core0_adrout), .in1(Core1_adrout), .out(multiplexer_3_out), .sel(and_6_out));
  ROM #(.addrWidth(14)) BIOS (.addr(multiplexer_3_out), .data(BIOS_data));
  TTY #(.cols(64), .rows(16)) tty_1 (.data(bit_extender_1_out), .clk(clock_1_out), .we(t_ff_1_q), .clr(or_6_out));
  T_Flip_Flop #(.trigger("falling")) t_ff_1 (.T(or_5_out), .clk(clock_1_out), .Q(t_ff_1_q));  // open: Qn, reset, preset
  and and_7 (and_7_out, Core1_wrtmem, comparator_3_eq, multiplexer_2_out);
  Comparator #(.mode("unsigned"), .width(16)) comparator_3 (
    .a({Core1_adrout_2, Core1_adrout}), .b(16'h400f), .eq(comparator_3_eq));  // open: gt, lt
  Comparator #(.mode("unsigned"), .width(16)) comparator_4 (
    .a(16'h400f), .b({Core0_adrout_2, Core0_adrout}), .eq(comparator_4_eq));  // open: gt, lt
  or or_6 (or_6_out, pull_resistor_5_node[0], pull_resistor_6_node[0]);
  Pull_Resistor pull_resistor_5 (.node({pull_resistor_5_node_2, pull_resistor_5_node[0]}));
  Pull_Resistor pull_resistor_6 (.node({pull_resistor_6_node_2, pull_resistor_6_node[0]}));
  assign {pull_resistor_5_node_2, pull_resistor_5_node[0]} = and_7_out ? Core1_dataout : 8'bz;  // Controlled_Buffer controlled_buffer_3
  assign {pull_resistor_6_node_2, pull_resistor_6_node[0]} = and_8_out ? Core0_dataout : 8'bz;  // Controlled_Buffer controlled_buffer_4
  and and_8 (and_8_out, Core0_wrtmem, comparator_4_eq, multiplexer_1_out);
  assign pull_resistor_1_node = and_9_out ? BIOS_data : 8'bz;  // Controlled_Buffer controlled_buffer_5
  and and_9 (and_9_out, Core0_ldmem, nor_1_out, multiplexer_1_out);
  assign pull_resistor_2_node = and_10_out ? BIOS_data : 8'bz;  // Controlled_Buffer controlled_buffer_6
  and and_10 (and_10_out, Core1_ldmem, nor_2_out, multiplexer_2_out);
  LED Core0Active (.in(multiplexer_1_out));
  LED Core1Active (.in(multiplexer_2_out));
  Comparator #(.mode("unsigned"), .width(16)) comparator_5 (
    .a({Core1_adrout_2, Core1_adrout}), .b(16'h4010), .eq(comparator_5_eq));  // open: gt, lt
  Comparator #(.mode("unsigned"), .width(16)) comparator_6 (
    .a(16'h4010), .b({Core0_adrout_2, Core0_adrout}), .eq(comparator_6_eq));  // open: gt, lt
  and and_11 (and_11_out, Core0_adrout_2[1], ~Core0_adrout[0], multiplexer_1_out, Core0_wrtmem);  // AND_Gate
  Multiplexer #(.width(8)) multiplexer_4 (
    .in0(Core0_dataout), .in1(Core1_dataout), .out(multiplexer_4_out), .sel(and_13_out));
  Keyboard keyboard_1 (.clk(clock_1_out), .re(t_ff_2_q), .data(keyboard_1_data));  // open: clr, avail
  and and_12 (and_12_out, Core1_wrtmem, comparator_5_eq, multiplexer_2_out);
  and and_13 (and_13_out, Core1_adrout_2[1], ~Core1_adrout[0], multiplexer_2_out, Core1_wrtmem);  // AND_Gate
  or or_7 (or_7_out, and_11_out, and_13_out);
  T_Flip_Flop #(.trigger("falling")) t_ff_2 (.T(or_8_out), .clk(clock_1_out), .Q(t_ff_2_q));  // open: Qn, reset, preset
  or or_8 (or_8_out, and_12_out, and_14_out);
  and and_14 (and_14_out, Core0_wrtmem, comparator_6_eq, multiplexer_1_out);
  and and_15 (and_15_out, Core1_adrout_2[1], ~Core1_adrout[0], multiplexer_2_out);  // AND_Gate
  Multiplexer #(.width(14)) multiplexer_5 (
    .in0({Core0_adrout_2[0], Core0_adrout[13:1]}), .in1({Core1_adrout_2[0], Core1_adrout[13:1]}),
    .out(multiplexer_5_out), .sel(and_15_out));
  RAM #(.addrWidth(14), .enables("line"), .\type ("nonvolatile")) MainMem0 (
    .addr(multiplexer_5_out), .we(or_7_out), .clk(clock_1_out), .din(multiplexer_4_out), .dout(MainMem0_dout));
  assign bit_extender_2_out = {{1{1'b0}}, keyboard_1_data};  // Bit_Extender bit_extender_2
  assign pull_resistor_2_node = and_12_out ? bit_extender_2_out : 8'bz;  // Controlled_Buffer controlled_buffer_7
  assign pull_resistor_1_node = and_14_out ? bit_extender_2_out : 8'bz;  // Controlled_Buffer controlled_buffer_8
  Comparator #(.mode("unsigned"), .width(16)) comparator_7 (
    .a({Core1_adrout_2, Core1_adrout}), .b(16'h4400), .eq(comparator_7_eq));  // open: gt, lt
  Comparator #(.mode("unsigned"), .width(16)) comparator_8 (
    .a(16'h4400), .b({Core0_adrout_2, Core0_adrout}), .eq(comparator_8_eq));  // open: gt, lt
  assign pull_resistor_1_node = and_16_out ? MainMem0_dout : 8'bz;  // Controlled_Buffer controlled_buffer_9
  and and_16 (and_16_out, Core0_adrout_2[1], ~Core0_adrout[0], multiplexer_1_out, Core0_ldmem);  // AND_Gate
  Register AtomCore1Low8 (.D(Core1_dataout), .en(and_17_out), .clk(clock_1_out), .Q(AtomCore1Low8_q));  // open: clr
  and and_17 (and_17_out, Core1_wrtmem, comparator_7_eq, multiplexer_2_out);
  Register AtomCore0Low8 (.D(Core0_dataout), .en(and_18_out), .clk(clock_1_out), .Q(AtomCore0Low8_q));  // open: clr
  and and_18 (and_18_out, Core0_wrtmem, comparator_8_eq, multiplexer_1_out);
  assign pull_resistor_2_node = and_19_out ? MainMem0_dout : 8'bz;  // Controlled_Buffer controlled_buffer_10
  and and_19 (and_19_out, Core1_adrout_2[1], ~Core1_adrout[0], multiplexer_2_out, Core1_ldmem);  // AND_Gate
  Multiplexer #(.width(8)) multiplexer_6 (
    .in0(Core0_dataout), .in1(Core1_dataout), .out(multiplexer_6_out), .sel(and_21_out));
  and and_20 (and_20_out, Core0_adrout_2[1], Core0_adrout[0], multiplexer_1_out, Core0_wrtmem);
  or or_9 (or_9_out, and_20_out, and_21_out);
  and and_21 (and_21_out, Core1_adrout_2[1], Core1_adrout[0], multiplexer_2_out, Core1_wrtmem);
  and and_22 (and_22_out, Core1_adrout_2[1], Core1_adrout[0], multiplexer_2_out);
  Comparator #(.mode("unsigned"), .width(16)) comparator_9 (
    .a({Core1_adrout_2, Core1_adrout}), .b(16'h4401), .eq(comparator_9_eq));  // open: gt, lt
  Comparator #(.mode("unsigned"), .width(16)) comparator_10 (
    .a(16'h4401), .b({Core0_adrout_2, Core0_adrout}), .eq(comparator_10_eq));  // open: gt, lt
  Multiplexer #(.width(14)) multiplexer_7 (
    .in0({Core0_adrout_2[0], Core0_adrout[13:1]}), .in1({Core1_adrout_2[0], Core1_adrout[13:1]}),
    .out(multiplexer_7_out), .sel(and_22_out));
  RAM #(.addrWidth(14), .enables("line"), .\type ("nonvolatile")) MainMem1 (
    .addr(multiplexer_7_out), .we(or_9_out), .clk(clock_1_out), .din(multiplexer_6_out), .dout(MainMem1_dout));
  and and_23 (and_23_out, Core1_wrtmem, comparator_9_eq, multiplexer_2_out);
  and and_24 (and_24_out, Core0_wrtmem, comparator_10_eq, multiplexer_1_out);
  Register AtomCore1High8 (.D(Core1_dataout), .en(and_23_out), .clk(clock_1_out), .Q(AtomCore1High8_q));  // open: clr
  Register AtomCore0High8 (.D(Core0_dataout), .en(and_24_out), .clk(clock_1_out), .Q(AtomCore0High8_q));  // open: clr
  assign pull_resistor_1_node = and_25_out ? MainMem1_dout : 8'bz;  // Controlled_Buffer controlled_buffer_11
  and and_25 (and_25_out, Core0_adrout_2[1], Core0_adrout[0], multiplexer_1_out, Core0_ldmem);
  assign pull_resistor_2_node = and_28_out ? MainMem1_dout : 8'bz;  // Controlled_Buffer controlled_buffer_12
  Comparator #(.mode("unsigned"), .width(16)) comparator_11 (
    .a({AtomCore1High8_q, AtomCore1Low8_q}), .b({Core0_adrout_2, Core0_adrout}), .eq(comparator_11_eq));  // open: gt, lt
  Comparator #(.mode("unsigned"), .width(16)) comparator_12 (
    .a({AtomCore1High8_q, AtomCore1Low8_q}), .b({AtomCore0High8_q, AtomCore0Low8_q}), .eq(comparator_12_eq));  // open: gt, lt
  Comparator #(.mode("unsigned"), .width(16)) comparator_13 (
    .a({AtomCore0High8_q, AtomCore0Low8_q}), .b({Core1_adrout_2, Core1_adrout}), .eq(comparator_13_eq));  // open: gt, lt
  and and_26 (and_26_out, comparator_12_eq, AtomCore0Ctr_q[0], and_31_out);
  and and_27 (and_27_out, comparator_13_eq, ~AtomCore1Ctr_q[0]);  // AND_Gate
  or or_10 (or_10_out, and_26_out, and_27_out);
  and and_28 (and_28_out, Core1_adrout_2[1], Core1_adrout[0], multiplexer_2_out, Core1_ldmem);
  and and_29 (and_29_out, comparator_12_eq, AtomCore1Ctr_q[0], and_32_out);
  and and_30 (and_30_out, comparator_11_eq, ~AtomCore0Ctr_q[0]);  // AND_Gate
  or or_11 (or_11_out, and_29_out, and_30_out);
  and and_31 (and_31_out, Core1_wrtmem, comparator_14_eq);
  Comparator #(.mode("unsigned"), .width(16)) comparator_14 (
    .a({Core1_adrout_2, Core1_adrout}), .b(16'h440f), .eq(comparator_14_eq));  // open: gt, lt
  and and_32 (and_32_out, Core0_wrtmem, comparator_15_eq);
  Comparator #(.mode("unsigned"), .width(16)) comparator_15 (
    .a({Core0_adrout_2, Core0_adrout}), .b(16'h440f), .eq(comparator_15_eq));  // open: gt, lt
  and and_33 (and_33_out, Core1_wrtmem, comparator_14_eq, multiplexer_2_out);
  and and_34 (and_34_out, Core0_wrtmem, comparator_15_eq, multiplexer_1_out);
  Register AtomCore1Ctr (.D(Core1_dataout), .en(and_33_out), .clk(clock_1_out), .Q(AtomCore1Ctr_q));  // open: clr
  Register AtomCore0Ctr (.D(Core0_dataout), .en(and_34_out), .clk(clock_1_out), .Q(AtomCore0Ctr_q));  // open: clr
endmodule

module PW_1A (
  input  [7:0] DataIn,
  input  Clk,
  input  CPUStop,
  input  CPUEn,
  output LdMem,
  output WrtMem,
  output [7:0] DataOut,
  output [15:0] AdrOut
);

  wire ADD_ADC_out, adder_2_cout, ALU_out, and_1_out, and_2_out, and_3_out, and_4_out, and_5_out, and_6_out,
       and_7_out, and_8_out, and_9_out, and_10_out, and_11_out, and_12_out, and_13_out, and_14_out, BIZ_out,
       BRANCH_out, CACT_out, CALL_out, CRY_q, decoder_1_out0, decoder_1_out1, decoder_1_out2, decoder_1_out3,
       decoder_2_out0, decoder_2_out1, decoder_2_out2, decoder_2_out3, JB_out, JBM_out, LDA_out, LDI_out,
       Load_out, MEM_out, MOV_out, nor_1_out, not_1_out, not_2_out, not_3_out, not_4_out, not_5_out,
       not_6_out, not_7_out, not_8_out, or_1_out, or_2_out, or_3_out, or_4_out, or_5_out, or_6_out, or_7_out,
       or_9_out, STRA_out, t_ff_1_q, t_ff_2_q, t_ff_2_qn, Write_out, xor_1_out;
  wire [1:0] CurrentOp_q_2, CurrentOp_q_3;
  wire [7:0] A_q, adder_1_out, adder_2_out, adder_2_out_2, B_q, C_q, multiplexer_3_out, multiplexer_4_out,
       multiplexer_5_out, multiplexer_7_out, multiplexer_8_out, multiplexer_10_out, multiplexer_11_out,
       nand_1_out, or_8_out, SEG_q, TA_q, TB_q, TC_q, TD_q, xor_2_out;
  wire [7:2] CurrentOp_q;
  wire [8:0] multiplexer_1_out, multiplexer_2_out;
  wire [8:8] adder_1_cout;
  wire [15:0] CTR_q, multiplexer_6_out;

  xor xor_1 (xor_1_out, CPUEn, adder_2_cout);
  T_Flip_Flop t_ff_1 (.T(and_1_out), .clk(Clk), .Q(t_ff_1_q), .reset(not_1_out));  // open: Qn, preset
  and and_1 (and_1_out, CPUStop, xor_1_out);
  and and_2 (and_2_out, CPUStop, t_ff_1_q);
  not not_1 (not_1_out, CPUEn);
  T_Flip_Flop t_ff_2 (.T(and_2_out), .clk(Clk), .Q(t_ff_2_q), .Qn(t_ff_2_qn), .reset(not_2_out));  // open: preset
  not not_2 (not_2_out, CPUEn);
  and Load (Load_out, and_2_out, xor_1_out, t_ff_2_qn);
  and Write (Write_out, and_2_out, xor_1_out, t_ff_2_q);
  Register CurrentOp (
    .D(DataIn), .en(Load_out), .clk(Clk), .Q({CurrentOp_q[7:5], CurrentOp_q_2, CurrentOp_q[2], CurrentOp_q_3}));  // open: clr
  nor MOV (MOV_out, CurrentOp_q[7], CurrentOp_q[6]);
  and LDI (LDI_out, CurrentOp_q[7], CurrentOp_q[6]);
  and ALU (ALU_out, ~CurrentOp_q[7], CurrentOp_q[6]);  // AND_Gate
  and JBM (JBM_out, CurrentOp_q[7], ~CurrentOp_q[6]);  // AND_Gate
  not not_3 (not_3_out, CurrentOp_q[7]);
  not not_4 (not_4_out, CurrentOp_q[5]);
  not not_5 (not_5_out, CurrentOp_q[2]);
  and MEM (MEM_out, JBM_out, not_4_out);
  and JB (JB_out, JBM_out, CurrentOp_q[5]);
  and CACT (CACT_out, ALU_out, Write_out);
  and LDA (LDA_out, MEM_out, not_5_out);
  and STRA (STRA_out, MEM_out, CurrentOp_q[2]);
  and BIZ (BIZ_out, JB_out, not_5_out);
  and CALL (CALL_out, or_3_out, Write_out);
  and ADD_ADC (ADD_ADC_out, CRY_q, CurrentOp_q[2]);
  Adder adder_1 (.a(DataOut), .b(or_8_out), .out(adder_1_out), .cin(ADD_ADC_out), .cout(adder_1_cout[8]));
  assign nand_1_out = ~(DataOut & or_8_out);  // NAND_Gate nand_1, 8 bits wide
  assign xor_2_out = DataOut ^ or_8_out;  // XOR_Gate xor_2, 8 bits wide
  Multiplexer #(.width(9)) multiplexer_1 (
    .in0({1'b1, nand_1_out}), .in1({1'b1, xor_2_out}), .out(multiplexer_1_out), .sel(CurrentOp_q[2]));
  nor nor_1 (nor_1_out, DataOut[0], DataOut[1], DataOut[2], DataOut[3], DataOut[5], DataOut[6], DataOut[7], DataOut[4]);
  and BRANCH (BRANCH_out, nor_1_out, BIZ_out);
  Multiplexer #(.width(9)) multiplexer_2 (
    .in0({adder_1_cout[8], adder_1_out}), .in1(multiplexer_1_out), .out(multiplexer_2_out),
    .sel(CurrentOp_q[5]));
  or or_1 (or_1_out, LDA_out, LDI_out);
  Multiplexer #(.width(8)) multiplexer_3 (
    .in0(or_8_out), .in1(multiplexer_2_out[7:0]), .out(multiplexer_3_out), .sel(ALU_out));
  or or_2 (or_2_out, not_3_out, CurrentOp_q[6], LDA_out);
  and and_3 (and_3_out, Write_out, ~and_6_out, or_2_out);  // AND_Gate
  and and_4 (and_4_out, xor_1_out, CPUStop, and_3_out);
  Decoder #(.select(2)) decoder_1 (
    .out0(decoder_1_out0), .out1(decoder_1_out1), .out2(decoder_1_out2), .out3(decoder_1_out3),
    .sel(CurrentOp_q_2), .en(and_4_out));
  Multiplexer #(.width(8)) multiplexer_4 (
    .in0(multiplexer_3_out), .in1(DataIn), .out(multiplexer_4_out), .sel(or_1_out));
  Multiplexer #(.width(8)) multiplexer_5 (.in0(DataOut), .in1(SEG_q), .out(multiplexer_5_out), .sel(BRANCH_out));
  and and_5 (and_5_out, xor_1_out, Write_out, and_6_out);
  Decoder #(.select(2)) decoder_2 (
    .out0(decoder_2_out0), .out1(decoder_2_out1), .out2(decoder_2_out2), .out3(decoder_2_out3),
    .sel(CurrentOp_q_2), .en(and_5_out));
  and and_6 (and_6_out, CurrentOp_q[5], MOV_out);
  not not_6 (not_6_out, not_5_out);
  and and_7 (and_7_out, JB_out, not_6_out);
  and and_8 (and_8_out, JB_out, BRANCH_out);
  or or_3 (or_3_out, and_7_out, and_8_out);
  or or_4 (or_4_out, or_3_out, LDI_out);
  and and_9 (and_9_out, or_4_out, Write_out);
  or or_5 (or_5_out, decoder_1_out1, CALL_out);
  or or_6 (or_6_out, decoder_1_out2, CALL_out);
  and and_10 (and_10_out, or_3_out, ~Load_out);  // AND_Gate
  Multiplexer #(.width(16)) multiplexer_6 (
    .in0({adder_2_out_2, adder_2_out}), .in1({multiplexer_5_out, or_8_out}), .out(multiplexer_6_out),
    .sel(and_10_out));
  and and_11 (and_11_out, xor_1_out, or_7_out);
  or or_7 (or_7_out, and_9_out, Load_out);
  Register A (.D(multiplexer_4_out), .en(decoder_1_out0), .clk(Clk), .Q(A_q));  // open: clr
  Register B (.D(multiplexer_7_out), .en(or_5_out), .clk(Clk), .Q(B_q));  // open: clr
  Multiplexer #(.width(8)) multiplexer_7 (
    .in0(multiplexer_4_out), .in1(adder_2_out), .out(multiplexer_7_out), .sel(CALL_out));
  Register C (.D(multiplexer_8_out), .en(or_6_out), .clk(Clk), .Q(C_q));  // open: clr
  Multiplexer #(.width(8)) multiplexer_8 (
    .in0(multiplexer_4_out), .in1(adder_2_out_2), .out(multiplexer_8_out), .sel(CALL_out));
  Register SEG (.D(multiplexer_4_out), .en(decoder_1_out3), .clk(Clk), .Q(SEG_q));  // open: clr
  Register TA (.D(multiplexer_4_out), .en(decoder_2_out0), .clk(Clk), .Q(TA_q));  // open: clr
  Register TB (.D(multiplexer_4_out), .en(decoder_2_out1), .clk(Clk), .Q(TB_q));  // open: clr
  Register TC (.D(multiplexer_4_out), .en(decoder_2_out2), .clk(Clk), .Q(TC_q));  // open: clr
  Register TD (.D(multiplexer_4_out), .en(decoder_2_out3), .clk(Clk), .Q(TD_q));  // open: clr
  Register #(.width(1)) CRY (.D(multiplexer_2_out[8]), .en(CACT_out), .clk(Clk), .Q(CRY_q));  // open: clr
  Register #(.width(16)) CTR (.D(multiplexer_6_out), .en(and_11_out), .clk(Clk), .Q(CTR_q), .clr(not_7_out));
  not not_7 (not_7_out, CPUEn);
  and and_12 (and_12_out, CurrentOp_q[2], MOV_out);
  Multiplexer #(.select(2), .width(8)) multiplexer_9 (
    .in0(A_q), .in1(B_q), .in2(C_q), .in3(SEG_q), .out(DataOut), .sel(CurrentOp_q_2));
  Adder #(.width(16)) adder_2 (
    .a(CTR_q), .b({16{1'b0}}), .out({adder_2_out_2, adder_2_out}), .cin(1'b1), .cout(adder_2_cout));
  not not_8 (not_8_out, and_12_out);
  Multiplexer #(.enable("true"), .select(2), .width(8)) multiplexer_10 (
    .in0(TA_q), .in1(TB_q), .in2(TC_q), .in3(TD_q), .out(multiplexer_10_out), .sel(CurrentOp_q_3),
    .en(and_12_out));
  assign or_8_out = multiplexer_11_out | multiplexer_10_out;  // OR_Gate or_8, 8 bits wide
  Multiplexer #(.enable("true"), .select(2), .width(8)) multiplexer_11 (
    .in0(A_q), .in1(B_q), .in2(C_q), .in3(SEG_q), .out(multiplexer_11_out), .sel(CurrentOp_q_3),
    .en(not_8_out));
  and and_13 (and_13_out, MEM_out, t_ff_2_q);
  Multiplexer #(.width(16)) multiplexer_12 (.in0(CTR_q), .in1({SEG_q, or_8_out}), .out(AdrOut), .sel(and_13_out));
  or or_9 (or_9_out, LDI_out, LDA_out);
  and and_14 (and_14_out, or_9_out, t_ff_2_q);
  and and_15 (WrtMem, STRA_out, t_ff_2_q);
  or or_10 (LdMem, t_ff_2_qn, and_14_out);
endmodule
